// Logisim project RSC.circ as structural Verilog: 10 circuits, main circuit Arith_U
module RSC (
  output [7:0] T,
  output [3:0] D
);

  wire control_1_acc_bus, control_1_acc_clr, control_1_acc_ld, control_1_ar_ld, control_1_dr_bus,
       control_1_dr_ld, control_1_ir_ld, control_1_outr_ld, control_1_pc_bus, control_1_pc_inc,
       control_1_pc_ld, control_1_r_bus, control_1_r_ld, control_1_ram_oe, control_1_ram_we, control_1_z_ld,
       Primary_Clock_out, z_reg_1_z_out;
  wire [2:0] control_1_alu_s;
  wire [3:0] outr_1_data_out, outr_1_data_out_2, outr_1_data_out_3, outr_1_data_out_4, outr_1_data_out_5,
       outr_1_data_out_6, outr_1_data_out_7, outr_1_data_out_8;
  wire [31:0] acc_1_data_out, alu_1_alu_out, ar_1_data_out, dr_1_data_out, ir_1_data_out, r_1_bus_out;

  Control control_1 (
    .Clock(Primary_Clock_out), .Z_In(z_reg_1_z_out), .IR_In(ir_1_data_out), .IR_LD(control_1_ir_ld),
    .RAM_WE(control_1_ram_we), .RAM_OE(control_1_ram_oe), .AR_LD(control_1_ar_ld), .PC_LD(control_1_pc_ld),
    .PC_INC(control_1_pc_inc), .T(T), .PC_BUS(control_1_pc_bus), .DR_LD(control_1_dr_ld),
    .DR_BUS(control_1_dr_bus), .R_LD(control_1_r_ld), .R_BUS(control_1_r_bus), .ACC_LD(control_1_acc_ld),
    .ACC_CLR(control_1_acc_clr), .ACC_BUS(control_1_acc_bus), .ALU_S(control_1_alu_s),
    .OUTR_LD(control_1_outr_ld), .Z_LD(control_1_z_ld), .D(D));
  Z_Reg z_reg_1 (.Clock(Primary_Clock_out), .ACC_in(acc_1_data_out), .Z_Load(control_1_z_ld), .Z_out(z_reg_1_z_out));
  Clock Primary_Clock (.out(Primary_Clock_out));
  ALU alu_1 (
    .A(acc_1_data_out), .B(r_1_bus_out), .S2(control_1_alu_s[2]), .S1(control_1_alu_s[1]),
    .S0(control_1_alu_s[0]), .ALU_Out(alu_1_alu_out));
  AR ar_1 (.Data_In(r_1_bus_out), .Load(control_1_ar_ld), .Clock(Primary_Clock_out), .Data_Out(ar_1_data_out));
  R r_1 (
    .Data_In(r_1_bus_out), .Load(control_1_r_ld), .Clock(Primary_Clock_out), .Bus_Enable(control_1_r_bus),
    .Bus_Out(r_1_bus_out));  // open: Data_Out
  RAM #(.addrWidth(16), .dataWidth(32), .databus("bidir"), .trigger("high")) ram_1 (
    .addr(ar_1_data_out[15:0]), .we(control_1_ram_we), .oe(control_1_ram_oe), .data(r_1_bus_out));
  // Probe on r_1_bus_out
  DR dr_1 (
    .Data_In(r_1_bus_out), .Load(control_1_dr_ld), .Clock(Primary_Clock_out), .Bus_Enable(control_1_dr_bus),
    .Data_Out(dr_1_data_out), .Bus_Out(r_1_bus_out));
  OUTR outr_1 (
    .Data_In(r_1_bus_out), .Load(control_1_outr_ld), .Clock(Primary_Clock_out),
    .Data_Out({outr_1_data_out_8, outr_1_data_out_7, outr_1_data_out_6, outr_1_data_out_5, outr_1_data_out_4, outr_1_data_out_3, outr_1_data_out_2, outr_1_data_out}));
  // Probe on acc_1_data_out
  PC pc_1 (
    .Data_In(r_1_bus_out), .Count(control_1_pc_inc), .Load(control_1_pc_ld), .Clock(Primary_Clock_out),
    .Bus_Enable(control_1_pc_bus), .Bus_Out(r_1_bus_out));  // open: Data_Out
  ACC acc_1 (
    .Data_In(alu_1_alu_out), .Load(control_1_acc_ld), .Clock(Primary_Clock_out), .Clear(control_1_acc_clr),
    .Bus_Enable(control_1_acc_bus), .Data_Out(acc_1_data_out), .Bus_Out(r_1_bus_out));
  Hex_Digit_Display hex_digit_display_1 (.value(outr_1_data_out_8));  // open: dp
  IR ir_1 (.Data_In(dr_1_data_out), .Load(control_1_ir_ld), .Clock(Primary_Clock_out), .Data_Out(ir_1_data_out));
  Hex_Digit_Display hex_digit_display_2 (.value(outr_1_data_out_7));  // open: dp
  Hex_Digit_Display hex_digit_display_3 (.value(outr_1_data_out_6));  // open: dp
  Hex_Digit_Display hex_digit_display_4 (.value(outr_1_data_out_5));  // open: dp
  Hex_Digit_Display hex_digit_display_5 (.value(outr_1_data_out_4));  // open: dp
  Hex_Digit_Display hex_digit_display_6 (.value(outr_1_data_out_3));  // open: dp
  Hex_Digit_Display hex_digit_display_7 (.value(outr_1_data_out_2));  // open: dp
  Hex_Digit_Display hex_digit_display_8 (.value(outr_1_data_out));  // open: dp

  // Notes on the sheet:
  //   Lisa Virden
  //   OLA8
  //   RSC
endmodule

// AU
module Arith_U (
  input  [31:0] A,
  input  [31:0] B,
  input  S1,
  input  S0,
  output [31:0] AU_out
);

  wire and_1_out, not_2_out;
  wire [31:0] adder_1_out, multiplexer_1_out, not_1_out, xor_1_out;

  assign xor_1_out = B ^ B;  // XOR_Gate xor_1, 32 bits wide
  assign not_1_out = ~B;  // NOT_Gate not_1, 32 bits wide
  Multiplexer #(.select(2), .width(32)) multiplexer_1 (
    .in0(not_1_out), .in1(B), .in2(xor_1_out), .in3(B), .out(multiplexer_1_out), .sel({S1, S0}));
  not not_2 (not_2_out, S0);
  Adder #(.width(32)) adder_1 (.a(A), .b(multiplexer_1_out), .out(adder_1_out), .cin(not_2_out));  // open: cout
  and and_1 (and_1_out, S1, S0);
  Multiplexer #(.width(32)) multiplexer_2 (.in0(adder_1_out), .in1(B), .out(AU_out), .sel(and_1_out));

  // Notes on the sheet:
  //   CLA4
  //   Arithmetic Unit
  //   Lisa Virden and Brady Welch - G 5
endmodule

// LU
module Logic_U (
  input  [31:0] A,
  input  [31:0] B,
  input  S1,
  input  S0,
  output [31:0] Logic_Out
);

  wire [31:0] and_1_out, not_1_out, or_1_out, shifter_1_out;

  assign and_1_out = A & B;  // AND_Gate and_1, 32 bits wide
  assign or_1_out = A | B;  // OR_Gate or_1, 32 bits wide
  Shifter #(.shift("ar"), .width(32)) shifter_1 (.in(A), .\dist (5'b00001), .out(shifter_1_out));
  assign not_1_out = ~A;  // NOT_Gate not_1, 32 bits wide
  Multiplexer #(.select(2), .width(32)) multiplexer_1 (
    .in0(and_1_out), .in1(or_1_out), .in2(shifter_1_out), .in3(not_1_out), .out(Logic_Out), .sel({S1, S0}));

  // Notes on the sheet:
  //   CLA5
  //   Logic Unit
  //   Lisa Virden and Brady Welch - G 5
endmodule

module ALU (
  input  [31:0] A,
  input  [31:0] B,
  input  S2,
  input  S1,
  input  S0,
  output [31:0] ALU_Out
);

  wire [31:0] arith_u_1_au_out, logic_u_1_logic_out;

  Arith_U arith_u_1 (.A(A), .B(B), .S1(S1), .S0(S0), .AU_out(arith_u_1_au_out));
  Multiplexer #(.width(32)) multiplexer_1 (.in0(arith_u_1_au_out), .in1(logic_u_1_logic_out), .out(ALU_Out), .sel(S2));
  Logic_U logic_u_1 (.A(A), .B(B), .S1(S1), .S0(S0), .Logic_Out(logic_u_1_logic_out));

  // Notes on the sheet:
  //   CLA5
  //   Lisa Virden and Brady Welch - G 5
  //   Arithmetic Logic Unit
endmodule

module SC (
  input  Clock,
  input  Clear,
  output [2:0] SEQ_out
);

  wire undriven;
  wire [2:0] adder_1_out;

  Adder #(.width(3)) adder_1 (.a(SEQ_out), .b(3'b001), .out(adder_1_out), .cin(undriven));  // open: cout
  Register #(.width(3)) register_1 (.D(adder_1_out), .en(1'b1), .clk(Clock), .Q(SEQ_out), .clr(Clear));

  // Notes on the sheet:
  //   CLA6
  //   Lisa Virden and Brady Welch - G 5
  //   Sequence Counter
endmodule

module DecoderCircuit (
  input  [31:0] IR_In,
  output [15:0] D_Out,
  output [3:0] Debug_Instruction
);

  wire not_1_out, or_1_out;

  Decoder #(.select(4)) decoder_1 (
    .out0(D_Out[0]), .out1(D_Out[1]), .out2(D_Out[2]), .out3(D_Out[3]), .out4(D_Out[4]), .out5(D_Out[5]),
    .out6(D_Out[6]), .out7(D_Out[7]), .out8(D_Out[8]), .out9(D_Out[9]), .out10(D_Out[10]), .out11(D_Out[11]),
    .out12(D_Out[12]), .out13(D_Out[13]), .out14(D_Out[14]), .out15(D_Out[15]), .sel(IR_In[3:0]),
    .en(not_1_out));
  or or_1 (or_1_out, IR_In[4], IR_In[5], IR_In[6], IR_In[7], IR_In[8], IR_In[9], IR_In[10], IR_In[11], IR_In[12], IR_In[13], IR_In[14], IR_In[15], IR_In[16], IR_In[17], IR_In[18], IR_In[19], IR_In[20], IR_In[21], IR_In[22], IR_In[23], IR_In[24], IR_In[25], IR_In[26], IR_In[27], IR_In[28], IR_In[29], IR_In[30], IR_In[31]);
  not not_1 (not_1_out, or_1_out);

  assign Debug_Instruction = IR_In[3:0];

  // Notes on the sheet:
  //   CLA7
  //   Lisa Virden and Brady Welch - G 5
  //   Decoder Circuit
endmodule

module TimerCircuit (
  input  Clock,
  input  Clear,
  input  Stop,
  output [7:0] T_Out
);

  wire not_1_out;
  wire [2:0] sc_1_seq_out;

  Decoder #(.select(3)) decoder_1 (
    .out0(T_Out[0]), .out1(T_Out[1]), .out2(T_Out[2]), .out3(T_Out[3]), .out4(T_Out[4]), .out5(T_Out[5]),
    .out6(T_Out[6]), .out7(T_Out[7]), .sel(sc_1_seq_out), .en(not_1_out));
  SC sc_1 (.Clock(Clock), .Clear(Clear), .SEQ_out(sc_1_seq_out));
  not not_1 (not_1_out, Stop);

  // Notes on the sheet:
  //   CLA7
  //   Timer Circuit
  //   Lisa Virden and Brady Welch - G 5
endmodule

module Z_Reg (
  input  Clock,
  input  [31:0] ACC_in,
  input  Z_Load,
  output Z_out
);

  wire not_1_out, or_1_out, or_2_out, or_3_out, or_4_out, or_5_out;

  or or_1 (or_1_out, ACC_in[0], ACC_in[1], ACC_in[2], ACC_in[3], ACC_in[4], ACC_in[5], ACC_in[6], ACC_in[7]);
  or or_2 (or_2_out, ACC_in[8], ACC_in[9], ACC_in[10], ACC_in[11], ACC_in[12], ACC_in[13], ACC_in[14], ACC_in[15]);
  or or_3 (or_3_out, ACC_in[16], ACC_in[17], ACC_in[18], ACC_in[19], ACC_in[20], ACC_in[21], ACC_in[22], ACC_in[23]);
  or or_4 (or_4_out, ACC_in[24], ACC_in[25], ACC_in[26], ACC_in[27], ACC_in[28], ACC_in[29], ACC_in[30], ACC_in[31]);
  or or_5 (or_5_out, or_1_out, or_2_out, or_3_out, or_4_out);
  not not_1 (not_1_out, or_5_out);
  Onebit_reg onebit_reg_1 (.Clock(Clock), .Data(not_1_out), .Clear(1'b0), .Load(Z_Load), .Data_Out(Z_out));

  // Notes on the sheet:
  //   Lisa Virden
  //   OLA7
  //   Z Register
endmodule

module Control (
  input  Clock,
  input  Z_In,
  input  [31:0] IR_In,
  output IR_LD,
  output RAM_WE,
  output RAM_OE,
  output AR_LD,
  output PC_LD,
  output PC_INC,
  output [7:0] T,
  output PC_BUS,
  output DR_LD,
  output DR_BUS,
  output R_LD,
  output R_BUS,
  output ACC_LD,
  output ACC_CLR,
  output ACC_BUS,
  output [2:0] ALU_S,
  output OUTR_LD,
  output Z_LD,
  output [3:0] D
);

  wire s_reg_1_data_out, scclr_1_sc_clr, sld_1_s_ld;
  wire [6:3] decodercircuit_1_d_out_2;
  wire [15:0] decodercircuit_1_d_out;

  S_Reg s_reg_1 (.Clock(Clock), .Data(1'b1), .Clear(1'b0), .Load(sld_1_s_ld), .Data_Out(s_reg_1_data_out));
  SCCLR scclr_1 (
    .t4(T[4]), .t5(T[5]), .t7(T[7]), .d1(decodercircuit_1_d_out_2[3]), .d2(decodercircuit_1_d_out_2[4]),
    .d5(decodercircuit_1_d_out_2[5]), .d6(decodercircuit_1_d_out_2[6]), .z(Z_In), .SC_CLR(scclr_1_sc_clr));
  SLD sld_1 (.t3(T[3]), .clock(Clock), .d0(decodercircuit_1_d_out[0]), .S_LD(sld_1_s_ld));
  TimerCircuit timercircuit_1 (.Clock(Clock), .Clear(scclr_1_sc_clr), .Stop(s_reg_1_data_out), .T_Out(T));
  DecoderCircuit decodercircuit_1 (
    .IR_In(IR_In),
    .D_Out({decodercircuit_1_d_out[15:7], decodercircuit_1_d_out_2[6:5], decodercircuit_1_d_out[4:3], decodercircuit_1_d_out_2[4:3], decodercircuit_1_d_out[0]}),
    .Debug_Instruction(D));
  IRLD irld_1 (.t2(T[2]), .clock(Clock), .IR_LD(IR_LD));
  RAMWE ramwe_1 (.t6(T[6]), .clock(Clock), .d2(decodercircuit_1_d_out_2[4]), .RAM_WE(RAM_WE));
  RAMOE ramoe_1 (
    .t1(T[1]), .t3(T[3]), .t5(T[5]), .d1(decodercircuit_1_d_out_2[3]), .d2(decodercircuit_1_d_out_2[4]),
    .d5(decodercircuit_1_d_out_2[5]), .d6(decodercircuit_1_d_out_2[6]), .z(Z_In), .RAM_OE(RAM_OE));
  ARLD arld_1 (
    .t0(T[0]), .t2(T[2]), .t4(T[4]), .clock(Clock), .d1(decodercircuit_1_d_out_2[3]),
    .d2(decodercircuit_1_d_out_2[4]), .AR_LD(AR_LD));
  PCLD pcld_1 (
    .t4(T[4]), .clock(Clock), .d5(decodercircuit_1_d_out_2[5]), .d6(decodercircuit_1_d_out_2[6]), .z(Z_In),
    .PC_LD(PC_LD));
  PCINC pcinc_1 (
    .t1(T[1]), .t3(T[3]), .clock(Clock), .d1(decodercircuit_1_d_out_2[3]), .d2(decodercircuit_1_d_out_2[4]),
    .d6(decodercircuit_1_d_out_2[6]), .z(Z_In), .PC_INC(PC_INC));
  PCBUS pcbus_1 (.t0(T[0]), .t2(T[2]), .PC_BUS(PC_BUS));
  DRLD drld_1 (
    .t1(T[1]), .t3(T[3]), .t5(T[5]), .clock(Clock), .d1(decodercircuit_1_d_out_2[3]),
    .d2(decodercircuit_1_d_out_2[4]), .d5(decodercircuit_1_d_out_2[5]), .d6(decodercircuit_1_d_out_2[6]),
    .z(Z_In), .DR_LD(DR_LD));
  DRBUS drbus_1 (
    .t4(T[4]), .t6(T[6]), .d1(decodercircuit_1_d_out_2[3]), .d2(decodercircuit_1_d_out_2[4]),
    .d5(decodercircuit_1_d_out_2[5]), .d6(decodercircuit_1_d_out_2[6]), .z(Z_In), .DR_BUS(DR_BUS));
  RLD rld_1 (.t3(T[3]), .clock(Clock), .d3(decodercircuit_1_d_out[3]), .R_LD(R_LD));
  RBUS rbus_1 (
    .t3(T[3]), .d4(decodercircuit_1_d_out[4]), .d8(decodercircuit_1_d_out[8]),
    .d9(decodercircuit_1_d_out[9]), .d12(decodercircuit_1_d_out[12]), .d13(decodercircuit_1_d_out[13]),
    .R_BUS(R_BUS));
  ACCLD accld_1 (
    .t3(T[3]), .t6(T[6]), .clock(Clock), .d1(decodercircuit_1_d_out_2[3]), .d4(decodercircuit_1_d_out[4]),
    .d8(decodercircuit_1_d_out[8]), .d9(decodercircuit_1_d_out[9]), .d10(decodercircuit_1_d_out[10]),
    .d12(decodercircuit_1_d_out[12]), .d13(decodercircuit_1_d_out[13]), .d14(decodercircuit_1_d_out[14]),
    .d15(decodercircuit_1_d_out[15]), .ACC_LD(ACC_LD));
  ACCCLR accclr_1 (.t3(T[3]), .d11(decodercircuit_1_d_out[11]), .ACC_CLR(ACC_CLR));
  ACCBUS accbus_1 (
    .t3(T[3]), .t5(T[5]), .d2(decodercircuit_1_d_out_2[4]), .d3(decodercircuit_1_d_out[3]),
    .d7(decodercircuit_1_d_out[7]), .ACC_BUS(ACC_BUS));
  ALU_SEL alu_sel_1 (
    .d1(decodercircuit_1_d_out_2[3]), .d4(decodercircuit_1_d_out[4]), .d9(decodercircuit_1_d_out[9]),
    .d10(decodercircuit_1_d_out[10]), .d12(decodercircuit_1_d_out[12]), .d13(decodercircuit_1_d_out[13]),
    .d14(decodercircuit_1_d_out[14]), .d15(decodercircuit_1_d_out[15]), .S2(ALU_S[2]), .S1(ALU_S[1]),
    .S0(ALU_S[0]));
  OUTRLD outrld_1 (.t3(T[3]), .clock(Clock), .d7(decodercircuit_1_d_out[7]), .OUTR_LD(OUTR_LD));
  ZLD zld_1 (.Z_LD(Z_LD));

  // Notes on the sheet:
  //   Lisa Virden
  //   OLA7
  //   Control Unit
  //   T
  //   D
endmodule

module S_Reg (
  input  Clock,
  input  Data,
  input  Clear,
  input  Load,
  output Data_Out
);

  wire and_1_out, and_2_out, not_1_out;

  and and_1 (and_1_out, Data, Load);
  not not_1 (not_1_out, Data);
  and and_2 (and_2_out, not_1_out, Load);
  J_K_Flip_Flop j_k_ff_1 (
    .J(and_1_out), .K(and_2_out), .clk(Clock), .Q(Data_Out), .preset(1'b0), .reset(Clear));  // open: Qn

  // Notes on the sheet:
  //   OLA7
  //   S-Reg
  //   Lisa Virden
endmodule
